# Fritzing sketch turret_wiring (saved by Fritzing 0.9.3b)
breadboards: 1

parts:
  Part1 = Arduino Uno (Rev3)
  J2 = Basic Servo
  J3 = Basic Servo
  U1 = 4-Channel 5v Relay Shield [package=relay-4ch5v10a]
  Part2 = Arduino Uno (Rev3)
  ANT1 = Antenna  # not connected

nets:
  N1: Part1.A4/SDA, Part2.A4/SDA
  N2: Part1.A5/SCL, Part2.A5/SCL
  N3: Part1.D3_PWM, J3.pulse
  N4: Part1.D4, J2.pulse
  N5: Part1.D7, U1.IN4
  VCC: Part1.5V, J2.vcc, J3.vcc, U1.VCC
  GND: Part1.GND, J2.gnd, J3.gnd, U1.GND, Part2.GND
  N6: U1.K3-On, U1.IN3

notes:
  Pan and Tilt servos
  Note: A remote powersource for the servos is recommended.
  BASE Module Uno
  (I2C Master)
  TURRET Module Uno
  (I2C Slave)
  Calico Home Security System
  - TURRET MODULE -
  Turret Relays
  Gun Placeholder

custom parts:
  4-Channel 5v Relay Shield: 4 Channel 5v Relay Shield w. 2x SPD-06VDC-SD-C
