# Fritzing sketch wifi_wiring (saved by Fritzing 0.9.3b)

parts:
  Part1 = Arduino Uno (Rev3)
  U1 = ESP8266 WiFi Module [part_number=ESP8266]

nets:
  N1: Part1.D10_PWM/SS, U1.TXD
  N2: Part1.D11_PWM/MOSI, U1.RXD
  3V3: Part1.3V3, U1.VCC, U1.CH_PD
  GND: Part1.GND, U1.GND

notes:
  Calico Home Security System
  - WIFI MODULE -

custom parts:
  ESP8266 WiFi Module: Generic WiFi Module based on the ESP8266 with onboard PCB antenna and UART communications
